// Logisim project 21071003高立扬.circ as structural Verilog: 13 circuits, main circuit main
module main (
  input  IFU_rst,
  input  GPR_clear,
  input  DM_clear
);

  wire _21071003_ALU_zero, clk, controller_1_alusrc, controller_1_j, controller_1_memtoreg,
       controller_1_memwr, controller_1_npc_sel, controller_1_regdst, controller_1_regwr;
  wire [1:0] controller_1_aluctr, controller_1_extop;
  wire [4:0] ifu_1_rd, ifu_1_rs, ifu_1_rt, multiplexer_1_out;
  wire [5:0] ifu_1_funct, ifu_1_opcode;
  wire [15:0] ifu_1_imm;
  wire [31:0] _21071003_ALU_out, _21071003_DM_busw, _21071003_EXT_out, ins, multiplexer_2_out, rd_rt, rs, rt;

  Multiplexer #(.select(1), .width(5), .disabled("Z"), .enable("false")) multiplexer_1 (
    .in0(ifu_1_rt), .in1(ifu_1_rd), .out(multiplexer_1_out), .sel(controller_1_regdst));
  Clock #(.highDuration(1), .lowDuration(1)) clock_1 (.out(clk));
  GPR gpr_1 (
    .busW(rd_rt), .rd_rt(multiplexer_1_out), .busA(rs), .busB(rt), .clk(clk), .rs(ifu_1_rs),
    .RegWr(controller_1_regwr), .rt(ifu_1_rt), .clear(GPR_clear));
  EXT _21071003_EXT (.imm(ifu_1_imm), .out(_21071003_EXT_out), .ExtOp(controller_1_extop));
  // Probe on ins
  Multiplexer #(.select(1), .width(32), .disabled("Z"), .enable("false")) multiplexer_2 (
    .in0(rt), .in1(_21071003_EXT_out), .out(multiplexer_2_out), .sel(controller_1_alusrc));
  // Probe on ins
  ALU _21071003_ALU (
    .ALU_SEL(controller_1_aluctr), .OUT(_21071003_ALU_out), .A(rs), .B(multiplexer_2_out),
    .ZERO(_21071003_ALU_zero));
  IFU ifu_1 (
    .clk(clk), .OpCode(ifu_1_opcode), .rs(ifu_1_rs), .rt(ifu_1_rt), .rd(ifu_1_rd), .funct(ifu_1_funct),
    .reset(IFU_rst), .nPC_sel(controller_1_npc_sel), .zero(_21071003_ALU_zero), .j(controller_1_j),
    .imm(ifu_1_imm), .command(ins));  // open: shamt
  DM _21071003_DM (
    .clk(clk), .clear(DM_clear), .data_in(rt), .MemWr(controller_1_memwr), .Addr(_21071003_ALU_out),
    .busW(_21071003_DM_busw));
  Multiplexer #(.select(1), .width(32), .disabled("Z"), .enable("false")) multiplexer_3 (
    .in0(_21071003_ALU_out), .in1(_21071003_DM_busw), .out(rd_rt), .sel(controller_1_memtoreg));
  Controller controller_1 (
    .nPC_sel(controller_1_npc_sel), .MemtoReg(controller_1_memtoreg), .MemWr(controller_1_memwr),
    .funct(ifu_1_funct), .opcode(ifu_1_opcode), .ALUctr(controller_1_aluctr), .RegDst(controller_1_regdst),
    .RegWr(controller_1_regwr), .ExtOp(controller_1_extop), .j(controller_1_j), .ALUSrc(controller_1_alusrc));
  // Probe on rs
  // Probe on ifu_1_rs
  // Probe on ifu_1_rt
  // Probe on rt
  // Probe on ifu_1_rd
  // Probe on rt

  // Notes on the sheet:
  //   (rs)
  //   (rt)
  //   busB/imm
  //   数据展示区
endmodule

module ALU (
  input  [1:0] ALU_SEL,
  input  [31:0] A,
  input  [31:0] B,
  output [31:0] OUT,
  output ZERO
);

  wire [31:0] \n32位并行加法器_1_s , \n32位并行加法器_2_s , not_1_out, or_1_out;

  Multiplexer #(.select(2), .width(32), .disabled("Z"), .enable("false")) multiplexer_1 (
    .in0(\n32位并行加法器_1_s ), .in1(\n32位并行加法器_2_s ), .in2(or_1_out), .out(OUT), .sel(ALU_SEL));  // open: in3
  \_32位并行加法器  \u_32位并行加法器_1  (.C0(1'b0), .S(\n32位并行加法器_1_s ), .A(A), .B(B));  // open: C16
  \_32位并行加法器  \u_32位并行加法器_2  (.C0(1'b1), .S(\n32位并行加法器_2_s ), .A(A), .B(not_1_out));  // open: C16
  assign not_1_out = ~B;  // NOT_Gate not_1, 32 bits wide
  assign or_1_out = A | B;  // OR_Gate or_1, 32 bits wide
  nor nor_1 (ZERO, OUT[31], OUT[30], OUT[29], OUT[28], OUT[27], OUT[26], OUT[25], OUT[24], OUT[23], OUT[22], OUT[21], OUT[20], OUT[19], OUT[18], OUT[17], OUT[16], OUT[14], OUT[13], OUT[12], OUT[11], OUT[10], OUT[9], OUT[8], OUT[7], OUT[6], OUT[5], OUT[4], OUT[3], OUT[2], OUT[1], OUT[0], OUT[15]);
endmodule

module EXT (
  input  [15:0] imm,
  input  [1:0] ExtOp,
  output [31:0] out
);

  wire [31:0] bit_extender_1_out, bit_extender_2_out;

  assign bit_extender_1_out = {{16{1'b0}}, imm};  // Bit_Extender bit_extender_1
  assign bit_extender_2_out = {{16{imm[15]}}, imm};  // Bit_Extender bit_extender_2
  Multiplexer #(.select(2), .width(32), .disabled("Z"), .enable("false")) multiplexer_1 (
    .in0(bit_extender_1_out), .in1(bit_extender_2_out), .in2({imm, {16{1'b0}}}), .out(out), .sel(ExtOp));  // open: in3
endmodule

// 21071003-GPR
module GPR (
  input  clk,
  input  [31:0] busW,
  input  [4:0] rs,
  input  [4:0] rt,
  input  clear,
  input  [4:0] rd_rt,
  input  RegWr,
  output [31:0] busA,
  output [31:0] busB
);

  wire undriven, w0, w1, w2, w3, w4, w5, w6, w7, w8, w9, w10, w11, w12, w13, w14, w15, w16, w17, w18, w19,
       w20, w21, w22, w23, w24, w25, w26, w27, w28, w29, w30, w31;
  wire [31:0] _0, _1, _2, _3, _4, _5, _6, _7, _8, _9, _10, _11, _12, _13, _14, _15, _16, _17, _19, _20, _21,
       _22, _23, _24, _26, _27, _28, _29, _30, _31;

  Multiplexer #(.select(5), .width(32), .disabled("Z"), .enable("false")) multiplexer_1 (
    .in0(_0), .in1(_1), .in2(_2), .in3(_3), .in4(_4), .in5(_5), .in6(_6), .in7(_7), .in8(_8), .in9(_9),
    .in10(_10), .in11(_11), .in12(_12), .in13(_13), .in14(_14), .in15(_15), .in16(_16), .in17(_17),
    .in18(_17), .in19(_19), .in20(_20), .in21(_21), .in22(_22), .in23(_23), .in24(_24), .in25(_24),
    .in26(_26), .in27(_27), .in28(_28), .in29(_29), .in30(_30), .in31(_31), .out(busA), .sel(rs));
  Multiplexer #(.select(5), .width(32), .disabled("Z"), .enable("false")) multiplexer_2 (
    .in0(_0), .in1(_1), .in2(_2), .in3(_3), .in4(_4), .in5(_5), .in6(_6), .in7(_7), .in8(_8), .in9(_9),
    .in10(_10), .in11(_11), .in12(_12), .in13(_13), .in14(_14), .in15(_15), .in16(_16), .in17(_17),
    .in18(_17), .in19(_19), .in20(_20), .in21(_21), .in22(_22), .in23(_23), .in24(_24), .in25(_24),
    .in26(_26), .in27(_27), .in28(_28), .in29(_29), .in30(_30), .in31(_31), .out(busB), .sel(rt));
  Demultiplexer #(.select(5), .width(1), .tristate("false"), .disabled("Z"), .enable("false")) demultiplexer_1 (
    .out0(w0), .out1(w1), .out2(w2), .out3(w3), .out4(w4), .out5(w5), .out6(w6), .out7(w7), .out8(w8),
    .out9(w9), .out10(w10), .out11(w11), .out12(w12), .out13(w13), .out14(w14), .out15(w15), .out16(w16),
    .out17(w17), .out18(w18), .out19(w19), .out20(w20), .out21(w21), .out22(w22), .out23(w23), .out24(w24),
    .out25(w25), .out26(w26), .out27(w27), .out28(w28), .out29(w29), .out30(w30), .out31(w31), .in(RegWr),
    .sel(rd_rt));
  Register #(.width(32), .trigger("rising"), .Select("low")) _0_zero (
    .D(busW), .en(w0), .Q(_0), .clk(clk), .clr(clear));
  Register #(.width(32), .trigger("rising"), .Select("low")) _1_at (.D(busW), .en(w1), .Q(_1), .clk(clk), .clr(clear));
  Register #(.width(32), .trigger("rising"), .Select("low")) _3_v1 (.D(busW), .en(w3), .Q(_3), .clk(clk), .clr(clear));
  Register #(.width(32), .trigger("rising"), .Select("low")) _2_v0 (.D(busW), .en(w2), .Q(_2), .clk(clk), .clr(clear));
  Register #(.width(32), .trigger("rising"), .Select("low")) _5_a1 (.D(busW), .en(w5), .Q(_5), .clk(clk), .clr(clear));
  Register #(.width(32), .trigger("rising"), .Select("low")) _4_a0 (.D(busW), .en(w4), .Q(_4), .clk(clk), .clr(clear));
  Register #(.width(32), .trigger("rising"), .Select("low")) _7_a3 (.D(busW), .en(w7), .Q(_7), .clk(clk), .clr(clear));
  Register #(.width(32), .trigger("rising"), .Select("low")) _6_a2 (.D(busW), .en(w6), .Q(_6), .clk(clk), .clr(clear));
  Register #(.width(32), .trigger("rising"), .Select("low")) _8_t0 (.D(busW), .en(w8), .Q(_8), .clk(clk), .clr(clear));
  Register #(.width(32), .trigger("rising"), .Select("low")) _10_t2 (
    .D(busW), .en(w10), .Q(_10), .clk(clk), .clr(clear));
  Register #(.width(32), .trigger("rising"), .Select("low")) _12_t4 (
    .D(busW), .en(w12), .Q(_12), .clk(clk), .clr(clear));
  Register #(.width(32), .trigger("rising"), .Select("low")) _14_t6 (
    .D(busW), .en(w14), .Q(_14), .clk(clk), .clr(clear));
  Register #(.width(32), .trigger("rising"), .Select("low")) _9_t1 (.D(busW), .en(w9), .Q(_9), .clk(clk), .clr(clear));
  Register #(.width(32), .trigger("rising"), .Select("low")) _11_t3 (
    .D(busW), .en(w11), .Q(_11), .clk(clk), .clr(clear), .cs(undriven));  // open: preset
  Register #(.width(32), .trigger("rising"), .Select("low")) _13_t5 (
    .D(busW), .en(w13), .Q(_13), .clk(clk), .clr(clear));
  Register #(.width(32), .trigger("rising"), .Select("low")) _15_t7 (
    .D(busW), .en(w15), .Q(_15), .clk(clk), .clr(clear));
  Register #(.width(32), .trigger("rising"), .Select("low")) _17_s1 (
    .D(busW), .en(w17), .Q(_17), .clk(clk), .clr(clear));
  Register #(.width(32), .trigger("rising"), .Select("low")) _18_s2 (
    .D(busW), .en(w16), .Q(_17), .clk(clk), .clr(clear));
  Register #(.width(32), .trigger("rising"), .Select("low")) _20_s4 (
    .D(busW), .en(w20), .Q(_20), .clk(clk), .clr(clear));
  Register #(.width(32), .trigger("rising"), .Select("low")) _22_s6 (
    .D(busW), .en(w22), .Q(_22), .clk(clk), .clr(clear));
  Register #(.width(32), .trigger("rising"), .Select("low")) _16_s0 (
    .D(busW), .en(w16), .Q(_16), .clk(clk), .clr(clear));
  Register #(.width(32), .trigger("rising"), .Select("low")) _19_s3 (
    .D(busW), .en(w19), .Q(_19), .clk(clk), .clr(clear));
  Register #(.width(32), .trigger("rising"), .Select("low")) _21_s5 (
    .D(busW), .en(w21), .Q(_21), .clk(clk), .clr(clear));
  Register #(.width(32), .trigger("rising"), .Select("low")) _23_s7 (
    .D(busW), .en(w23), .Q(_23), .clk(clk), .clr(clear));
  Register #(.width(32), .trigger("rising"), .Select("low")) _24_t8 (
    .D(busW), .en(w24), .Q(_24), .clk(clk), .clr(clear));
  Register #(.width(32), .trigger("rising"), .Select("low")) _26_k0 (
    .D(busW), .en(w26), .Q(_26), .clk(clk), .clr(clear));
  Register #(.width(32), .trigger("rising"), .Select("low")) _28_gp (
    .D(busW), .en(w28), .Q(_28), .clk(clk), .clr(clear));
  Register #(.width(32), .trigger("rising"), .Select("low")) _30_fp (
    .D(busW), .en(w30), .Q(_30), .clk(clk), .clr(clear));
  Register #(.width(32), .trigger("rising"), .Select("low")) _25_t9 (
    .D(busW), .en(w25), .Q(_24), .clk(clk), .clr(clear));
  Register #(.width(32), .trigger("rising"), .Select("low")) _27_k1 (
    .D(busW), .en(w27), .Q(_27), .clk(clk), .clr(clear));
  Register #(.width(32), .trigger("rising"), .Select("low")) _29_sp (
    .D(busW), .en(w29), .Q(_29), .clk(clk), .clr(clear));
  Register #(.width(32), .trigger("rising"), .Select("low")) _31_ra (
    .D(busW), .en(w31), .Q(_31), .clk(clk), .clr(clear));

  // Other names for the same wires on the sheet: _18[31:0] = _17; _25[31:0] = _24
endmodule

// 21071003-IM
module IM (
  input  [31:0] PC,
  output [31:0] command,
  output [5:0] OpCode,
  output [4:0] rs,
  output [4:0] rt,
  output [4:0] rd,
  output [4:0] shamt,
  output [5:0] funct,
  output [15:0] imm
);

  ROM #(.addrWidth(8), .dataWidth(8), .Select("low")) _3 (.addr(PC[9:2]), .data(command[31:24]));
  ROM #(.addrWidth(8), .dataWidth(8), .Select("low")) _2 (.addr(PC[9:2]), .data(command[23:16]));
  ROM #(.addrWidth(8), .dataWidth(8), .Select("low")) _1 (.addr(PC[9:2]), .data(command[15:8]));
  ROM #(.addrWidth(8), .dataWidth(8), .Select("low")) _0 (.addr(PC[9:2]), .data(command[7:0]));
  // Probe on command

  assign funct = command[5:0];
  assign imm = command[15:0];
  assign OpCode = command[31:26];
  assign rd = command[15:11];
  assign rs = command[25:21];
  assign rt = command[20:16];
  assign shamt = command[10:6];

  // Notes on the sheet:
  //   beq分支，只需改变第二条指令最低2位为02/06
  //   contents of _3 (hex, n*v repeats v):
  //   4*34 ac 1 11 1 3c 8c 1 34 ad 8 ad 34 34 ad 1 34 ac
  //   contents of _2 (hex, n*v repeats v):
  //   9 a b c c 2a 8b 2a 9 a 2a b 69 0 b c b 6c 8b d d
  //   contents of _1 (hex, n*v repeats v):
  //   5*0 60 0 48 0 0 48 0 0 c 4*0 60 7
  //   contents of _0 (hex, n*v repeats v):
  //   4 2 a 6 0 21 7 21 1 0 21 20 0 12 0 7b 1c 0 21 e7 24
endmodule

module DM (
  input  clk,
  input  clear,
  input  [31:0] data_in,
  input  MemWr,
  input  [31:0] Addr,
  output [31:0] busW
);

  RAM #(.addrWidth(8), .dataWidth(8), .bus("separate"), .Select("low")) _4 (
    .addr(Addr[9:2]), .din(data_in[31:24]), .data(busW[31:24]), .str(MemWr), .clk(clk), .clr(clear));  // open: sel, ld
  RAM #(.addrWidth(8), .dataWidth(8), .bus("separate"), .Select("low")) _3 (
    .addr(Addr[9:2]), .din(data_in[23:16]), .data(busW[23:16]), .str(MemWr), .clk(clk), .clr(clear));  // open: sel, ld
  RAM #(.addrWidth(8), .dataWidth(8), .bus("separate"), .Select("low")) _2 (
    .addr(Addr[9:2]), .din(data_in[15:8]), .data(busW[15:8]), .str(MemWr), .clk(clk), .clr(clear));  // open: sel, ld
  RAM #(.addrWidth(8), .dataWidth(8), .bus("separate"), .Select("low")) _1 (
    .addr(Addr[9:2]), .din(data_in[7:0]), .data(busW[7:0]), .str(MemWr), .clk(clk), .clr(clear));  // open: sel, ld
endmodule

// 21071003-IFU
module IFU (
  input  j,
  input  nPC_sel,
  input  zero,
  input  clk,
  input  reset,
  output [31:0] command,
  output [5:0] OpCode,
  output [4:0] rs,
  output [4:0] rt,
  output [4:0] rd,
  output [4:0] shamt,
  output [5:0] funct,
  output [15:0] imm
);

  wire and_1_out;
  wire [27:0] alu_1_out;
  wire [31:0] alu_2_out, bit_extender_1_out, multiplexer_1_out, multiplexer_2_out, PC_q, shifter_1_out;
  wire [31:28] j_32;

  assign bit_extender_1_out = {{16{imm[15]}}, imm};  // Bit_Extender bit_extender_1
  ALU alu_1 (.ALU_SEL(2'b00), .OUT({j_32, alu_1_out}), .A(PC_q), .B(32'h4));  // open: ZERO
  Shifter #(.width(32), .shift("ll")) shifter_1 (.in(bit_extender_1_out), .\dist (5'b00010), .out(shifter_1_out));
  and and_1 (and_1_out, nPC_sel, zero);
  ALU alu_2 (.ALU_SEL(2'b00), .OUT(alu_2_out), .A({j_32, alu_1_out}), .B(shifter_1_out));  // open: ZERO
  Multiplexer #(.select(1), .width(32), .disabled("Z"), .enable("false")) multiplexer_1 (
    .in0({j_32, alu_1_out}), .in1(alu_2_out), .out(multiplexer_1_out), .sel(and_1_out));
  Multiplexer #(.select(1), .width(32), .disabled("Z"), .enable("false")) multiplexer_2 (
    .in0(multiplexer_1_out), .in1({j_32, rs, rt, imm, 2'b00}), .out(multiplexer_2_out), .sel(j));
  Register #(.width(32), .trigger("rising"), .Select("low")) PC (
    .D(multiplexer_2_out), .Q(PC_q), .clk(clk), .clr(reset));  // open: en
  IM im_1 (
    .PC(PC_q), .OpCode(OpCode), .rs(rs), .rt(rt), .rd(rd), .shamt(shamt), .funct(funct), .imm(imm),
    .command(command));
  // Probe on imm
  // Probe on {rs, rt, imm}
  // Probe on {j_32, rs, rt, imm, 2'b00}

  // Other names for the same wires on the sheet: j_32[27:2] = {rs, rt, imm}; PC_31_28[3:0] = j_32
endmodule

// 21071003-Controller
module Controller (
  input  [5:0] funct,
  input  [5:0] opcode,
  output RegDst,
  output RegWr,
  output [1:0] ALUctr,
  output [1:0] ExtOp,
  output ALUSrc,
  output nPC_sel,
  output MemtoReg,
  output MemWr,
  output j
);

  wire addu, F0N, F1N, F2N, F3N, F4N, F5N, O0N, O1N, O2N, O3N, O4N, O5N, subu;

  not not_1 (F0N, funct[0]);
  not not_2 (F1N, funct[1]);
  not not_3 (F2N, funct[2]);
  not not_4 (F3N, funct[3]);
  not not_5 (F4N, funct[4]);
  not not_6 (F5N, funct[5]);
  and and_1 (addu, O0N, O1N, O2N, O3N, O4N, O5N, funct[5], F4N, F3N, F2N, F1N, funct[0]);
  and and_2 (ALUctr[1], opcode[0], O1N, opcode[2], O4N, O5N, opcode[3]);
  and and_3 (MemtoReg, opcode[0], opcode[1], O2N, O4N, opcode[5], O3N);
  and and_4 (ExtOp[1], opcode[0], opcode[1], opcode[2], O4N, O5N, opcode[3]);
  not not_7 (O3N, opcode[3]);
  not not_8 (O4N, opcode[4]);
  not not_9 (O5N, opcode[5]);
  not not_10 (O2N, opcode[2]);
  not not_11 (O1N, opcode[1]);
  not not_12 (O0N, opcode[0]);
  and and_5 (subu, O0N, O1N, O2N, O3N, O4N, O5N, funct[5], F4N, F3N, F2N, funct[1], funct[0]);
  and and_6 (nPC_sel, O0N, O1N, opcode[2], O4N, O5N, O3N);
  and and_7 (MemWr, opcode[0], opcode[1], O2N, O4N, opcode[5], opcode[3]);
  and and_8 (j, O0N, opcode[1], O2N, O4N, O5N, O3N);
  or or_1 (RegDst, addu, subu);
  or or_2 (ALUctr[0], subu, nPC_sel);
  or or_3 (ALUSrc, MemtoReg, MemWr, ALUctr[1], ExtOp[1]);
  or or_4 (RegWr, addu, subu, ALUctr[1], MemtoReg, ExtOp[1]);
  or or_5 (ExtOp[0], MemtoReg, MemWr);

  // Other names for the same wires on the sheet: ori = ALUctr[1]; beq = nPC_sel; lui = ExtOp[1]; F0 = funct[0];
  //   F1 = funct[1]; F2 = funct[2]; F3 = funct[3]; F4 = funct[4]; F5 = funct[5]; lw = MemtoReg; O0 = opcode[0];
  //   O1 = opcode[1]; O2 = opcode[2]; O3 = opcode[3]; O4 = opcode[4]; O5 = opcode[5]; sw = MemWr

  // Notes on the sheet:
  //   数据分割部分
  //   单个指令识别
  //   剩余指令发出部分
endmodule

// 21071003-组间加法器
module \组间并行加法器  (
  input  G3,
  input  G2,
  input  G1,
  input  G0,
  input  P3,
  input  P2,
  input  P1,
  input  P0,
  input  C0,
  output C1,
  output C2,
  output C3,
  output C4
);

  wire and_1_out, and_2_out, and_3_out, and_4_out, and_5_out, and_6_out, and_7_out, and_8_out, and_9_out,
       and_10_out;

  or or_1 (C1, and_1_out, G0);
  or or_2 (C3, and_2_out, and_3_out, and_4_out, G2);
  and and_1 (and_1_out, P0, C0);
  and and_2 (and_2_out, P2, P1, P0, C0);
  and and_3 (and_3_out, P2, P1, G0);
  and and_4 (and_4_out, P2, G1);
  or or_3 (C2, and_5_out, and_6_out, G1);
  or or_4 (C4, and_7_out, and_8_out, and_9_out, G3, and_10_out);
  and and_5 (and_5_out, P1, P0, C0);
  and and_6 (and_6_out, P1, G0);
  and and_7 (and_7_out, P3, P2, P1, P0, C0);
  and and_8 (and_8_out, P3, P2, P1, G0);
  and and_9 (and_9_out, P3, P2, G1);
  and and_10 (and_10_out, P3, G2);
endmodule

// 21071003-组内并行
module \组内并行加法器  (
  input  C0,
  input  [3:0] A,
  input  [3:0] B,
  output S1,
  output S2,
  output S3,
  output S4,
  output P1_star,
  output G1_star
);

  wire and_1_out, and_2_out, and_3_out, and_4_out, and_8_out, and_9_out, and_10_out, and_11_out, and_12_out,
       G0, G1, G2, G3, or_1_out, or_2_out, or_4_out, P0, P1, P2, P3;

  xor xor_1 (S1, C0, P0);
  xor xor_2 (S2, P1, or_1_out);
  xor xor_3 (S3, or_4_out, P2);
  xor xor_4 (S4, or_2_out, P3);
  // Probe on or_1_out
  or or_1 (or_1_out, and_1_out, G0);
  // Probe on or_2_out
  or or_2 (or_2_out, and_2_out, and_3_out, and_4_out, G2);
  and and_1 (and_1_out, P0, C0);
  and and_2 (and_2_out, P2, P1, P0, C0);
  and and_3 (and_3_out, P2, P1, G0);
  and and_4 (and_4_out, P2, G1);
  and and_5 (P1_star, P3, P2, P1, P0);
  or or_3 (G1_star, and_10_out, and_11_out, and_12_out, G3);
  xor xor_5 (P3, A[3], B[3]);
  and and_6 (G3, B[3], A[3]);
  // Probe on or_4_out
  or or_4 (or_4_out, and_8_out, and_9_out, G1);
  and and_7 (G2, B[2], A[2]);
  xor xor_6 (P2, A[2], B[2]);
  and and_8 (and_8_out, P1, P0, C0);
  and and_9 (and_9_out, P1, G0);
  and and_10 (and_10_out, P3, P2, P1, G0);
  and and_11 (and_11_out, P3, P2, G1);
  and and_12 (and_12_out, G2, P3);
  and and_13 (G1, B[1], A[1]);
  xor xor_7 (P1, A[1], B[1]);
  and and_14 (G0, B[0], A[0]);
  xor xor_8 (P0, A[0], B[0]);
endmodule

// 21071003-16位加法器
module \_16位并行加法器  (
  input  C0,
  input  [15:0] A,
  input  [15:0] B,
  output [15:0] S,
  output C16
);

  wire _1_4_g1_star, _1_4_p1_star, _5_8_g1_star, _5_8_p1_star, _9_12_g1_star, _9_12_p1_star, _13_16_g1_star,
       _13_16_p1_star, \组间并行加法器_1_c1 , \组间并行加法器_1_c2 , \组间并行加法器_1_c3 ;

  \组内并行加法器  _1_4 (
    .S1(S[0]), .S2(S[1]), .S3(S[2]), .S4(S[3]), .P1_star(_1_4_p1_star), .G1_star(_1_4_g1_star), .A(A[3:0]),
    .B(B[3:0]), .C0(C0));
  \组内并行加法器  _5_8 (
    .S1(S[4]), .S2(S[5]), .S3(S[6]), .S4(S[7]), .P1_star(_5_8_p1_star), .G1_star(_5_8_g1_star), .A(A[7:4]),
    .B(B[7:4]), .C0(\组间并行加法器_1_c1 ));
  \组间并行加法器  \u_组间并行加法器_1  (
    .C1(\组间并行加法器_1_c1 ), .C2(\组间并行加法器_1_c2 ), .C3(\组间并行加法器_1_c3 ), .C4(C16), .C0(C0), .G3(_13_16_g1_star),
    .G2(_9_12_g1_star), .G1(_5_8_g1_star), .G0(_1_4_g1_star), .P3(_13_16_p1_star), .P2(_9_12_p1_star),
    .P1(_5_8_p1_star), .P0(_1_4_p1_star));
  \组内并行加法器  _9_12 (
    .S1(S[8]), .S2(S[9]), .S3(S[10]), .S4(S[11]), .P1_star(_9_12_p1_star), .G1_star(_9_12_g1_star),
    .A(A[11:8]), .B(B[11:8]), .C0(\组间并行加法器_1_c2 ));
  \组内并行加法器  _13_16 (
    .S1(S[12]), .S2(S[13]), .S3(S[14]), .S4(S[15]), .P1_star(_13_16_p1_star), .G1_star(_13_16_g1_star),
    .A(A[15:12]), .B(B[15:12]), .C0(\组间并行加法器_1_c3 ));
endmodule

// 21071003-32位加法器
module \_32位并行加法器  (
  input  C0,
  input  [31:0] B,
  input  [31:0] A,
  output C16,
  output [31:0] S
);

  wire _1_16_c16;

  \_16位并行加法器  _1_16 (.C0(C0), .S(S[15:0]), .C16(_1_16_c16), .A(A[15:0]), .B(B[15:0]));
  \_16位并行加法器  _17_32 (.C0(_1_16_c16), .S(S[31:16]), .C16(C16), .A(A[31:16]), .B(B[31:16]));
endmodule

module \IFU示范  (
  input  nPC_sel,
  input  zero,
  input  clk,
  input  reset,
  output [31:0] instruction
);

  wire and_1_out;
  wire [31:0] adder_1_out, adder_2_out, bit_extender_1_out, multiplexer_1_out, PC_q, shifter_1_out;

  assign bit_extender_1_out = {{16{instruction[15]}}, instruction[15:0]};  // Bit_Extender bit_extender_1
  Shifter #(.width(32), .shift("ll")) shifter_1 (.in(bit_extender_1_out), .\dist (5'b00010), .out(shifter_1_out));
  Adder #(.width(32)) adder_1 (.a(PC_q), .b(32'h4), .out(adder_1_out));  // open: cin, cout
  Adder #(.width(32)) adder_2 (.a(adder_1_out), .b(shifter_1_out), .out(adder_2_out));  // open: cin, cout
  Multiplexer #(.select(1), .width(32), .disabled("Z"), .enable("false")) multiplexer_1 (
    .in0(adder_1_out), .in1(adder_2_out), .out(multiplexer_1_out), .sel(and_1_out));
  and and_1 (and_1_out, nPC_sel, zero);
  Register #(.width(32), .trigger("rising"), .Select("low")) PC (
    .D(multiplexer_1_out), .Q(PC_q), .clk(clk), .clr(reset));  // open: en
  ROM #(.addrWidth(8), .dataWidth(8), .Select("low")) _3 (.addr(PC_q[9:2]), .data(instruction[31:24]));
  ROM #(.addrWidth(8), .dataWidth(8), .Select("low")) _2 (.addr(PC_q[9:2]), .data(instruction[23:16]));
  ROM #(.addrWidth(8), .dataWidth(8), .Select("low")) _1 (.addr(PC_q[9:2]), .data(instruction[15:8]));
  ROM #(.addrWidth(8), .dataWidth(8), .Select("low")) _0 (.addr(PC_q[9:2]), .data(instruction[7:0]));
  // Probe on instruction

  // Other names for the same wires on the sheet: imm[15:0] = instruction[15:0]

  // Notes on the sheet:
  //   34010001
  //   34010002
  //   00221821
  //   ac030008
  //   上高位下低位
  //   8位16进制指令，从高位到低位2位2位存
  //   contents of _3 (hex, n*v repeats v):
  //   34 34 0 ac
  //   contents of _2 (hex, n*v repeats v):
  //   1 2 22 3
  //   contents of _1 (hex, n*v repeats v):
  //   0 0 18
  //   contents of _0 (hex, n*v repeats v):
  //   1 2 21 18
endmodule
