// Logisim project ComputerOrganizaion.circ as structural Verilog: 16 circuits, main circuit 头文件
module main (
  input  [3:0] A,
  input  [3:0] B,
  output P1,
  output G1,
  output P2,
  output G2,
  output P3,
  output G3,
  output P4,
  output G4
);

  xor xor_1 (P1, A[0], B[0]);
  and and_1 (G1, A[0], B[0]);
  xor xor_2 (P2, A[1], B[1]);
  and and_2 (G2, A[1], B[1]);
  xor xor_3 (P3, A[2], B[2]);
  and and_3 (G3, A[2], B[2]);
  xor xor_4 (P4, A[3], B[3]);
  and and_4 (G4, A[3], B[3]);
endmodule

module \并行四位加法器  (
  input  C0,
  input  [3:0] A,
  input  [3:0] B,
  output S1,
  output S2,
  output S3,
  output S4,
  output P1_star,
  output G1_star
);

  wire and_1_out, and_2_out, and_3_out, and_4_out, and_5_out, and_6_out, and_8_out, and_9_out, and_10_out,
       main_1_g1, main_1_g2, main_1_g3, main_1_g4, main_1_p1, main_1_p2, main_1_p3, main_1_p4, or_1_out,
       or_2_out, or_3_out;

  xor xor_1 (S1, C0, main_1_p1);
  and and_1 (and_1_out, C0, main_1_p1);
  or or_1 (or_1_out, and_1_out, main_1_g1);
  xor xor_2 (S2, or_1_out, main_1_p2);
  and and_2 (and_2_out, main_1_p1, C0, main_1_p2);
  or or_2 (or_2_out, and_2_out, and_3_out, main_1_g2);
  and and_3 (and_3_out, main_1_g1, main_1_p2);
  main main_1 (
    .P1(main_1_p1), .G1(main_1_g1), .P2(main_1_p2), .G2(main_1_g2), .P3(main_1_p3), .G3(main_1_g3),
    .P4(main_1_p4), .G4(main_1_g4), .A(A), .B(B));
  xor xor_3 (S3, or_2_out, main_1_p3);
  or or_3 (or_3_out, and_5_out, and_4_out, and_6_out, main_1_g3);
  and and_4 (and_4_out, main_1_p2, main_1_g1, main_1_p3);
  and and_5 (and_5_out, main_1_p1, main_1_p2, C0, main_1_p3);
  xor xor_4 (S4, or_3_out, main_1_p4);
  and and_6 (and_6_out, main_1_g2, main_1_p3);
  and and_7 (P1_star, main_1_p4, main_1_p1, main_1_p2, main_1_p3);
  or or_4 (G1_star, and_8_out, and_9_out, and_10_out, main_1_g4);
  and and_8 (and_8_out, main_1_p2, main_1_p3, main_1_p4, main_1_g1);
  and and_9 (and_9_out, main_1_p4, main_1_p3, main_1_g2);
  and and_10 (and_10_out, main_1_p4, main_1_g3);
endmodule

module \组间并行加法器  (
  input  C0,
  input  G1_star,
  input  P1_star,
  input  G2_star,
  input  P2_star,
  input  G3_star,
  input  P3_star,
  input  G4_star,
  input  P4_star,
  output C4,
  output C8,
  output C12,
  output C16
);

  wire and_1_out, and_2_out, and_3_out, and_4_out, and_5_out, and_6_out, and_7_out, and_8_out, and_9_out,
       and_10_out;

  and and_1 (and_1_out, C0, P1_star);
  or or_1 (C4, and_1_out, G1_star);
  and and_2 (and_2_out, P1_star, C0, P2_star);
  or or_2 (C8, and_3_out, and_2_out, G2_star);
  and and_3 (and_3_out, G1_star, P2_star);
  and and_4 (and_4_out, P1_star, C0, P2_star, P3_star);
  and and_5 (and_5_out, P3_star, G2_star);
  and and_6 (and_6_out, P2_star, P3_star, G1_star);
  or or_3 (C12, and_4_out, and_6_out, and_5_out, G3_star);
  and and_7 (and_7_out, P1_star, P2_star, P3_star, C0, P4_star);
  and and_8 (and_8_out, G1_star, P2_star, P3_star, P4_star);
  or or_4 (C16, and_7_out, and_8_out, and_9_out, and_10_out, G4_star);
  and and_9 (and_9_out, G2_star, P3_star, P4_star);
  and and_10 (and_10_out, G3_star, P4_star);
endmodule

module \_16位加法器  (
  input  in_1,
  input  [15:0] A,
  input  [15:0] B,
  output C1,
  output [15:0] S1
);

  wire \并行四位加法器_1_g1_star , \并行四位加法器_1_p1_star , \并行四位加法器_2_g1_star , \并行四位加法器_2_p1_star ,
       \并行四位加法器_3_g1_star , \并行四位加法器_3_p1_star , \并行四位加法器_4_g1_star , \并行四位加法器_4_p1_star , \组间并行加法器_1_c4 ,
       \组间并行加法器_1_c8 , \组间并行加法器_1_c12 ;

  \并行四位加法器  \u_并行四位加法器_1  (
    .C0(in_1), .S1(S1[0]), .S2(S1[1]), .S3(S1[2]), .S4(S1[3]), .P1_star(\并行四位加法器_1_p1_star ),
    .G1_star(\并行四位加法器_1_g1_star ), .A(A[3:0]), .B(B[3:0]));
  \并行四位加法器  \u_并行四位加法器_2  (
    .C0(\组间并行加法器_1_c4 ), .S1(S1[4]), .S2(S1[5]), .S3(S1[6]), .S4(S1[7]), .P1_star(\并行四位加法器_2_p1_star ),
    .G1_star(\并行四位加法器_2_g1_star ), .A(A[7:4]), .B(B[7:4]));
  \组间并行加法器  \u_组间并行加法器_1  (
    .C0(in_1), .C4(\组间并行加法器_1_c4 ), .C8(\组间并行加法器_1_c8 ), .C12(\组间并行加法器_1_c12 ), .C16(C1),
    .G1_star(\并行四位加法器_1_g1_star ), .P1_star(\并行四位加法器_1_p1_star ), .G2_star(\并行四位加法器_2_g1_star ),
    .P2_star(\并行四位加法器_2_p1_star ), .G3_star(\并行四位加法器_3_g1_star ), .P3_star(\并行四位加法器_3_p1_star ),
    .G4_star(\并行四位加法器_4_g1_star ), .P4_star(\并行四位加法器_4_p1_star ));
  \并行四位加法器  \u_并行四位加法器_3  (
    .C0(\组间并行加法器_1_c8 ), .S1(S1[8]), .S2(S1[9]), .S3(S1[10]), .S4(S1[11]), .P1_star(\并行四位加法器_3_p1_star ),
    .G1_star(\并行四位加法器_3_g1_star ), .A(A[11:8]), .B(B[11:8]));
  \并行四位加法器  \u_并行四位加法器_4  (
    .C0(\组间并行加法器_1_c12 ), .S1(S1[12]), .S2(S1[13]), .S3(S1[14]), .S4(S1[15]), .P1_star(\并行四位加法器_4_p1_star ),
    .G1_star(\并行四位加法器_4_g1_star ), .A(A[15:12]), .B(B[15:12]));
endmodule

module \_32位加法器  (
  input  C0,
  input  [31:0] A,
  input  [31:0] B,
  output C1,
  output [31:0] S
);

  wire \n16位加法器_1_c1 ;

  \_16位加法器  \u_16位加法器_1  (.in_1(C0), .S1(S[15:0]), .C1(\n16位加法器_1_c1 ), .A(A[15:0]), .B(B[15:0]));
  \_16位加法器  \u_16位加法器_2  (.in_1(\n16位加法器_1_c1 ), .S1(S[31:16]), .C1(C1), .A(A[31:16]), .B(B[31:16]));
endmodule

module \_32位或运算器  (
  input  [31:0] A,
  input  [31:0] B,
  output [31:0] S
);

  assign S = A | B;  // OR_Gate or_1, 32 bits wide
endmodule

module \_32位ALU  (
  input  [1:0] in_1,
  input  [31:0] A,
  input  [31:0] B,
  output out_4,
  output [31:0] out_5
);

  wire [31:0] \n32位减法器_1_s , \n32位加法器_1_s , \n32位或运算器_1_s ;

  Multiplexer #(.select(2), .width(32), .disabled("Z"), .enable("true")) multiplexer_1 (
    .in0(\n32位加法器_1_s ), .in1(\n32位减法器_1_s ), .in2(\n32位或运算器_1_s ), .out(out_5), .sel(in_1), .en(1'b1));  // open: in3
  \_32位加法器  \u_32位加法器_1  (.C0(1'b0), .S(\n32位加法器_1_s ), .A(A), .B(B));  // open: C1
  \_32位或运算器  \u_32位或运算器_1  (.S(\n32位或运算器_1_s ), .A(A), .B(B));
  Zero zero_1 (.in_1(out_5), .out_2(out_4));
  \_32位减法器  \u_32位减法器_1  (.S(\n32位减法器_1_s ), .A(A), .B(B));  // open: C1
endmodule

module \_32位减法器  (
  input  [31:0] A,
  input  [31:0] B,
  output C1,
  output [31:0] S
);

  wire \n16位加法器_1_c1 ;
  wire [15:0] not_1_out, not_1_out_2;

  \_16位加法器  \u_16位加法器_1  (.in_1(1'b1), .S1(S[15:0]), .C1(\n16位加法器_1_c1 ), .A(A[15:0]), .B(not_1_out));
  \_16位加法器  \u_16位加法器_2  (.in_1(\n16位加法器_1_c1 ), .S1(S[31:16]), .C1(C1), .A(A[31:16]), .B(not_1_out_2));
  assign {not_1_out_2, not_1_out} = ~B;  // NOT_Gate not_1, 32 bits wide
endmodule

module \符号扩展器  (
  input  [15:0] in_1,
  input  [1:0] in_2,
  output [31:0] out_3
);

  wire [31:0] bit_extender_1_out, bit_extender_2_out;

  assign bit_extender_1_out = {{16{1'b0}}, in_1};  // Bit_Extender bit_extender_1
  assign bit_extender_2_out = {{16{in_1[15]}}, in_1};  // Bit_Extender bit_extender_2
  Multiplexer #(.select(2), .width(32), .disabled("Z"), .enable("false")) multiplexer_1 (
    .in0(bit_extender_1_out), .in1(bit_extender_2_out), .in2({in_1, {16{1'b0}}}), .out(out_3), .sel(in_2));  // open: in3
endmodule

module \指令存储器  (
  input  [31:0] in_1,
  output [15:0] limit,
  output [5:0] funct,
  output [4:0] shamt,
  output [4:0] RD,
  output [4:0] RT,
  output [4:0] RS,
  output [5:0] OP
);

  ROM #(.addrWidth(8), .dataWidth(8), .Select("high")) rom_1 (.addr(in_1[9:2]), .data({OP, RS[4:3]}), .sel(1'b1));
  ROM #(.addrWidth(8), .dataWidth(8), .Select("high")) rom_2 (.addr(in_1[9:2]), .data({RS[2:0], RT}), .sel(1'b1));
  ROM #(.addrWidth(8), .dataWidth(8), .Select("high")) rom_3 (.addr(in_1[9:2]), .data(limit[15:8]), .sel(1'b1));
  ROM #(.addrWidth(8), .dataWidth(8), .Select("high")) rom_4 (.addr(in_1[9:2]), .data({limit[7:6], funct}), .sel(1'b1));

  assign limit[5:0] = funct;
  assign RD = limit[15:11];
  assign shamt = limit[10:6];

  // Notes on the sheet:
  //   contents of rom_1 (hex, n*v repeats v):
  //   34 34 0 0 1 ac 8c 11 3c 8 34 3c 8
  //   contents of rom_2 (hex, n*v repeats v):
  //   3 6 66 66 2a 9 a 2a b 10 b 9 10
  //   contents of rom_3 (hex, n*v repeats v):
  //   0 0 40 48 4*0 cd 0 ef 45
  //   contents of rom_4 (hex, n*v repeats v):
  //   93 ae 21 23 21 10 10 2 cd d ef 67 7
endmodule

module \控制器  (
  input  [5:0] func,
  input  [5:0] opcode,
  output MemtoReg,
  output MemWrite,
  output RegDst,
  output ALUSrc,
  output RegWrite,
  output nPC_sel,
  output [1:0] EXTop,
  output j,
  output [1:0] ALU_ctl
);

  wire addu, F1N, F2N, F3N, F4N, OP0N, OP1N, OP2N, OP3N, OP4N, OP5N, subu;

  not not_1 (F3N, func[3]);
  not not_2 (F4N, func[4]);
  or or_1 (RegDst, addu, subu);
  not not_3 (F2N, func[2]);
  not not_4 (OP0N, opcode[0]);
  not not_5 (OP1N, opcode[1]);
  not not_6 (OP2N, opcode[2]);
  not not_7 (OP3N, opcode[3]);
  not not_8 (F1N, func[1]);
  not not_9 (OP4N, opcode[4]);
  not not_10 (OP5N, opcode[5]);
  or or_2 (ALUSrc, ALU_ctl[1], MemtoReg, EXTop[1], MemWrite);
  or or_3 (EXTop[0], MemtoReg, MemWrite);
  or or_4 (RegWrite, addu, subu, EXTop[1], ALU_ctl[1], MemtoReg);
  or or_5 (ALU_ctl[0], nPC_sel, subu);
  and and_1 (addu, OP0N, OP1N, OP2N, OP3N, OP4N, OP5N, func[5], F4N, F3N, F2N, F1N, func[0]);
  and and_2 (subu, OP0N, OP1N, OP2N, OP3N, OP4N, OP5N, func[5], F4N, F3N, F2N, func[1], func[0]);
  and and_3 (ALU_ctl[1], opcode[0], OP1N, opcode[2], opcode[3], OP4N, OP5N);
  and and_4 (MemtoReg, opcode[0], opcode[1], OP2N, OP3N, OP4N, opcode[5]);
  and and_5 (MemWrite, opcode[0], opcode[1], OP2N, opcode[3], OP4N, opcode[5]);
  and and_6 (nPC_sel, OP0N, OP1N, opcode[2], OP3N, OP4N, OP5N);
  and and_7 (EXTop[1], opcode[0], opcode[1], opcode[2], opcode[3], OP4N, OP5N);
  and and_8 (j, OP0N, opcode[1], OP2N, OP3N, OP4N, OP5N);

  // Other names for the same wires on the sheet: ori = ALU_ctl[1]; beq = nPC_sel; lui = EXTop[1]; F0N = func[0];
  //   F1 = func[1]; F5 = func[5]; lw = MemtoReg; OP0 = opcode[0]; OP1 = opcode[1]; OP2 = opcode[2]; OP3 = opcode[3];
  //   OP5 = opcode[5]; sw = MemWrite
endmodule

module \_32_32寄存器  (
  input  [31:0] WriteData,
  input  in_2,
  input  in_3,
  input  RegWrite,
  input  [4:0] rs_in,
  input  [4:0] Wset,
  input  [4:0] rt_in,
  output [31:0] rs_out,
  output [31:0] rt_out
);

  wire w2, w3, w4, w5, w6, w7, w8, w9, w10, w11, w12, w13, w14, w15, w16, w17, w18, w19, w20, w21, w22, w23,
       w24, w25, w26, w27, w28, w29, w30, w31, w32;
  wire [31:0] _1, _2, _3, _4, _5, _6, _7, _8, _9, _10, _11, _12, _13, _14, _15, _16, _17, _18, _19, _20, _21,
       _22, _23, _24, _25, _26, _27, _28, _29, _30, _31, _32;

  Demultiplexer #(.select(5), .width(1), .tristate("false"), .disabled("Z"), .enable("true")) demultiplexer_1 (
    .out1(w2), .out2(w3), .out3(w4), .out4(w5), .out5(w6), .out6(w7), .out7(w8), .out8(w9), .out9(w10),
    .out10(w11), .out11(w12), .out12(w13), .out13(w14), .out14(w15), .out15(w16), .out16(w17), .out17(w18),
    .out18(w19), .out19(w20), .out20(w21), .out21(w22), .out22(w23), .out23(w24), .out24(w25), .out25(w26),
    .out26(w27), .out27(w28), .out28(w29), .out29(w30), .out30(w31), .out31(w32), .in(RegWrite), .sel(Wset),
    .en(1'b1));  // open: out0
  Register #(.width(32), .trigger("rising"), .Select("low")) register_1 (
    .D(WriteData), .en(1'b0), .Q(_1), .clk(in_2), .clr(in_3));
  Register #(.width(32), .trigger("rising"), .Select("low")) register_2 (
    .D(WriteData), .en(w2), .Q(_2), .clk(in_2), .clr(in_3), .preset(in_3));  // open: cs
  Register #(.width(32), .trigger("rising"), .Select("low")) register_3 (
    .D(WriteData), .en(w3), .Q(_3), .clk(in_2), .clr(in_3), .preset(in_3));  // open: cs
  Register #(.width(32), .trigger("rising"), .Select("low")) register_4 (
    .D(WriteData), .en(w4), .Q(_4), .clk(in_2), .clr(in_3), .preset(in_3));  // open: cs
  Register #(.width(32), .trigger("rising"), .Select("low")) register_5 (
    .D(WriteData), .en(w5), .Q(_5), .clk(in_2), .clr(in_3), .preset(in_3));  // open: cs
  Register #(.width(32), .trigger("rising"), .Select("low")) register_6 (
    .D(WriteData), .en(w6), .Q(_6), .clk(in_2), .clr(in_3), .preset(in_3));  // open: cs
  Register #(.width(32), .trigger("rising"), .Select("low")) register_7 (
    .D(WriteData), .en(w7), .Q(_7), .clk(in_2), .clr(in_3), .preset(in_3));  // open: cs
  Register #(.width(32), .trigger("rising"), .Select("low")) register_8 (
    .D(WriteData), .en(w8), .Q(_8), .clk(in_2), .clr(in_3), .preset(in_3));  // open: cs
  Register #(.width(32), .trigger("rising"), .Select("low")) register_9 (
    .D(WriteData), .en(w9), .Q(_9), .clk(in_2), .clr(in_3), .preset(in_3));  // open: cs
  Register #(.width(32), .trigger("rising"), .Select("low")) register_10 (
    .D(WriteData), .en(w10), .Q(_10), .clk(in_2), .clr(in_3), .preset(in_3));  // open: cs
  Register #(.width(32), .trigger("rising"), .Select("low")) register_11 (
    .D(WriteData), .en(w11), .Q(_11), .clk(in_2), .clr(in_3), .preset(in_3));  // open: cs
  Register #(.width(32), .trigger("rising"), .Select("low")) register_12 (
    .D(WriteData), .en(w12), .Q(_12), .clk(in_2), .clr(in_3), .preset(in_3));  // open: cs
  Register #(.width(32), .trigger("rising"), .Select("low")) register_13 (
    .D(WriteData), .en(w13), .Q(_13), .clk(in_2), .clr(in_3), .preset(in_3));  // open: cs
  Register #(.width(32), .trigger("rising"), .Select("low")) register_14 (
    .D(WriteData), .en(w14), .Q(_14), .clk(in_2), .clr(in_3), .preset(in_3));  // open: cs
  Register #(.width(32), .trigger("rising"), .Select("low")) register_15 (
    .D(WriteData), .en(w15), .Q(_15), .clk(in_2), .clr(in_3), .preset(in_3));  // open: cs
  Register #(.width(32), .trigger("rising"), .Select("low")) register_16 (
    .en(w16), .Q(_16), .clk(in_2), .clr(in_3), .preset(in_3));  // open: D, cs
  Register #(.width(32), .trigger("rising"), .Select("low")) register_17 (
    .D(WriteData), .en(w17), .Q(_17), .clk(in_2), .clr(in_3), .preset(in_3));  // open: cs
  Register #(.width(32), .trigger("rising"), .Select("low")) register_18 (
    .D(WriteData), .en(w18), .Q(_18), .clk(in_2), .clr(in_3), .preset(in_3));  // open: cs
  Register #(.width(32), .trigger("rising"), .Select("low")) register_19 (
    .D(WriteData), .en(w19), .Q(_19), .clk(in_2), .clr(in_3), .preset(in_3));  // open: cs
  Register #(.width(32), .trigger("rising"), .Select("low")) register_20 (
    .D(WriteData), .en(w20), .Q(_20), .clk(in_2), .clr(in_3), .preset(in_3));  // open: cs
  Register #(.width(32), .trigger("rising"), .Select("low")) register_21 (
    .D(WriteData), .en(w21), .Q(_21), .clk(in_2), .clr(in_3), .preset(in_3));  // open: cs
  Register #(.width(32), .trigger("rising"), .Select("low")) register_22 (
    .D(WriteData), .en(w22), .Q(_22), .clk(in_2), .clr(in_3), .preset(in_3));  // open: cs
  Register #(.width(32), .trigger("rising"), .Select("low")) register_23 (
    .D(WriteData), .en(w23), .Q(_23), .clk(in_2), .clr(in_3), .preset(in_3));  // open: cs
  Register #(.width(32), .trigger("rising"), .Select("low")) register_24 (
    .D(WriteData), .en(w24), .Q(_24), .clk(in_2), .clr(in_3), .preset(in_3));  // open: cs
  Register #(.width(32), .trigger("rising"), .Select("low")) register_25 (
    .D(WriteData), .en(w25), .Q(_25), .clk(in_2), .clr(in_3), .preset(in_3));  // open: cs
  Register #(.width(32), .trigger("rising"), .Select("low")) register_26 (
    .D(WriteData), .en(w26), .Q(_26), .clk(in_2), .clr(in_3), .preset(in_3));  // open: cs
  Register #(.width(32), .trigger("rising"), .Select("low")) register_27 (
    .D(WriteData), .en(w27), .Q(_27), .clk(in_2), .clr(in_3), .preset(in_3));  // open: cs
  Register #(.width(32), .trigger("rising"), .Select("low")) register_28 (
    .D(WriteData), .en(w28), .Q(_28), .clk(in_2), .clr(in_3), .preset(in_3));  // open: cs
  Register #(.width(32), .trigger("rising"), .Select("low")) register_29 (
    .D(WriteData), .en(w29), .Q(_29), .clk(in_2), .clr(in_3), .preset(in_3));  // open: cs
  Register #(.width(32), .trigger("rising"), .Select("low")) register_30 (
    .D(WriteData), .en(w30), .Q(_30), .clk(in_2), .clr(in_3), .preset(in_3));  // open: cs
  Register #(.width(32), .trigger("rising"), .Select("low")) register_31 (
    .D(WriteData), .en(w31), .Q(_31), .clk(in_2), .clr(in_3), .preset(in_3));  // open: cs
  Register #(.width(32), .trigger("rising"), .Select("low")) register_32 (
    .D(WriteData), .en(w32), .Q(_32), .clk(in_2), .clr(in_3), .preset(in_3));  // open: cs
  Multiplexer #(.select(5), .width(32), .disabled("Z"), .enable("true")) multiplexer_1 (
    .in0(_1), .in1(_2), .in2(_3), .in3(_4), .in4(_5), .in5(_6), .in6(_7), .in7(_8), .in8(_9), .in9(_10),
    .in10(_11), .in11(_12), .in12(_13), .in13(_14), .in14(_15), .in15(_16), .in16(_17), .in17(_18),
    .in18(_19), .in19(_20), .in20(_21), .in21(_22), .in22(_23), .in23(_24), .in24(_25), .in25(_26),
    .in26(_27), .in27(_28), .in28(_29), .in29(_30), .in30(_31), .in31(_32), .out(rs_out), .sel(rs_in),
    .en(1'b1));
  Multiplexer #(.select(5), .width(32), .disabled("Z"), .enable("true")) multiplexer_2 (
    .in0(_1), .in1(_2), .in2(_3), .in3(_4), .in4(_5), .in5(_6), .in6(_7), .in7(_8), .in8(_9), .in9(_10),
    .in10(_11), .in11(_12), .in12(_13), .in13(_14), .in14(_15), .in15(_16), .in16(_17), .in17(_18),
    .in18(_19), .in19(_20), .in20(_21), .in21(_22), .in22(_23), .in23(_24), .in24(_25), .in25(_26),
    .in26(_27), .in27(_28), .in28(_29), .in29(_30), .in30(_31), .in31(_32), .out(rt_out), .sel(rt_in),
    .en(1'b1));

  // Notes on the sheet:
  //   RegWrite: pull=down
endmodule

module \数据存储器  (
  input  clear,
  input  MenRead,
  input  in_3,
  input  [31:0] address,
  input  [31:0] \input ,
  output [31:0] out_6
);

  RAM #(.addrWidth(8), .dataWidth(8), .bus("separate"), .Select("high")) ram_1 (
    .addr(address[9:2]), .din(\input [31:24]), .data(out_6[31:24]), .str(MenRead), .clk(in_3), .clr(clear));  // open: sel, ld
  RAM #(.addrWidth(8), .dataWidth(8), .bus("separate"), .Select("high")) ram_2 (
    .addr(address[9:2]), .din(\input [23:16]), .data(out_6[23:16]), .str(MenRead), .clk(in_3), .clr(clear));  // open: sel, ld
  RAM #(.addrWidth(8), .dataWidth(8), .bus("separate"), .Select("high")) ram_3 (
    .addr(address[9:2]), .din(\input [15:8]), .data(out_6[15:8]), .str(MenRead), .clk(in_3), .clr(clear));  // open: sel, ld
  RAM #(.addrWidth(8), .dataWidth(8), .bus("separate"), .Select("high")) ram_4 (
    .addr(address[9:2]), .din(\input [7:0]), .data(out_6[7:0]), .str(MenRead), .clk(in_3), .clr(clear));  // open: sel, ld

  // Notes on the sheet:
  //   MenRead: pull=down
endmodule

module IFU (
  input  Jump,
  input  Clck,
  input  ZERO,
  input  nPC_sel,
  input  Reset,
  output [15:0] out_6,
  output [4:0] out_7,
  output [4:0] out_8,
  output [5:0] out_9,
  output [5:0] out_10,
  output [4:0] out_11,
  output [4:0] out_12
);

  wire and_1_out;
  wire [3:0] _1;
  wire [27:0] \n32位alu_1_out_5 ;
  wire [31:0] bit_extender_1_out, multiplexer_1_out, multiplexer_2_out, \n32位alu_2_out_5 , PC_q,
       shifter_1_out;

  Register #(.width(32), .trigger("rising"), .Select("low")) PC (
    .D(multiplexer_2_out), .Q(PC_q), .clk(Clck), .clr(Reset));  // open: en
  \指令存储器  \u_指令存储器_1  (
    .in_1(PC_q), .limit(out_6), .funct(out_10), .shamt(out_11), .RD(out_12), .RT(out_7), .RS(out_8),
    .OP(out_9));
  \_32位ALU  \u_32位alu_1  (.in_1(2'b00), .out_5({_1, \n32位alu_1_out_5 }), .A(PC_q), .B(32'h4));  // open: out_4
  \_32位ALU  \u_32位alu_2  (
    .in_1(2'b00), .out_5(\n32位alu_2_out_5 ), .A({_1, \n32位alu_1_out_5 }), .B(shifter_1_out));  // open: out_4
  assign bit_extender_1_out = {{16{out_6[15]}}, out_6};  // Bit_Extender bit_extender_1
  Shifter #(.width(32), .shift("ll")) shifter_1 (.in(bit_extender_1_out), .\dist (5'b00010), .out(shifter_1_out));
  Multiplexer #(.select(1), .width(32), .disabled("Z"), .enable("false")) multiplexer_1 (
    .in0({_1, \n32位alu_1_out_5 }), .in1(\n32位alu_2_out_5 ), .out(multiplexer_1_out), .sel(and_1_out));
  Multiplexer #(.select(1), .width(32), .disabled("Z"), .enable("false")) multiplexer_2 (
    .in0(multiplexer_1_out), .in1({_1, out_8, out_7, out_6, 2'b00}), .out(multiplexer_2_out), .sel(Jump));
  and and_1 (and_1_out, ZERO, nPC_sel);
endmodule

module Zero (
  input  [31:0] in_1,
  output out_2
);

  wire or_1_out;

  or or_1 (or_1_out, in_1[0], in_1[1], in_1[2], in_1[3], in_1[4], in_1[5], in_1[6], in_1[7], in_1[8], in_1[9], in_1[10], in_1[11], in_1[12], in_1[13], in_1[14], in_1[15], in_1[16], in_1[17], in_1[18], in_1[19], in_1[20], in_1[21], in_1[22], in_1[23], in_1[24], in_1[25], in_1[26], in_1[27], in_1[28], in_1[29], in_1[30], in_1[31]);
  not not_1 (out_2, or_1_out);
endmodule

module \头文件  (
  input  clear,
  input  clear_2,
  input  reset
);

  wire clck, \n32位alu_1_out_4 , \控制器_1_alusrc , \控制器_1_j , \控制器_1_memtoreg , \控制器_1_memwrite ,
       \控制器_1_npc_sel , \控制器_1_regdst , \控制器_1_regwrite ;
  wire [1:0] \控制器_1_alu_ctl , \控制器_1_extop ;
  wire [4:0] ifu_1_out_7, ifu_1_out_8, ifu_1_out_12, multiplexer_1_out;
  wire [5:0] ifu_1_out_9, ifu_1_out_10;
  wire [15:0] ifu_1_out_6;
  wire [31:0] multiplexer_2_out, multiplexer_3_out, \n32_32寄存器_1_rs_out , \n32_32寄存器_1_rt_out ,
       \n32位alu_1_out_5 , \数据存储器_1_out_6 , \符号扩展器_1_out_3 ;

  Clock #(.highDuration(1), .lowDuration(1)) u_clck (.out(clck));
  IFU ifu_1 (
    .Jump(\控制器_1_j ), .Clck(clck), .out_6(ifu_1_out_6), .Reset(reset), .out_9(ifu_1_out_9),
    .out_10(ifu_1_out_10), .out_12(ifu_1_out_12), .out_7(ifu_1_out_7), .out_8(ifu_1_out_8),
    .ZERO(\n32位alu_1_out_4 ), .nPC_sel(\控制器_1_npc_sel ));  // open: out_11
  \符号扩展器  \u_符号扩展器_1  (.out_3(\符号扩展器_1_out_3 ), .in_1(ifu_1_out_6), .in_2(\控制器_1_extop ));
  Multiplexer #(.select(1), .width(5), .disabled("Z"), .enable("false")) multiplexer_1 (
    .in0(ifu_1_out_7), .in1(ifu_1_out_12), .out(multiplexer_1_out), .sel(\控制器_1_regdst ));
  \_32_32寄存器  \u_32_32寄存器_1  (
    .WriteData(multiplexer_3_out), .RegWrite(\控制器_1_regwrite ), .Wset(multiplexer_1_out),
    .rs_out(\n32_32寄存器_1_rs_out ), .rt_out(\n32_32寄存器_1_rt_out ), .rs_in(ifu_1_out_8), .rt_in(ifu_1_out_7),
    .in_2(clck), .in_3(clear));
  \控制器  \u_控制器_1  (
    .func(ifu_1_out_10), .MemtoReg(\控制器_1_memtoreg ), .MemWrite(\控制器_1_memwrite ), .RegDst(\控制器_1_regdst ),
    .ALUSrc(\控制器_1_alusrc ), .RegWrite(\控制器_1_regwrite ), .nPC_sel(\控制器_1_npc_sel ), .EXTop(\控制器_1_extop ),
    .j(\控制器_1_j ), .ALU_ctl(\控制器_1_alu_ctl ), .opcode(ifu_1_out_9));
  Multiplexer #(.select(1), .width(32), .disabled("Z"), .enable("false")) multiplexer_2 (
    .in0(\n32_32寄存器_1_rt_out ), .in1(\符号扩展器_1_out_3 ), .out(multiplexer_2_out), .sel(\控制器_1_alusrc ));
  \_32位ALU  \u_32位alu_1  (
    .in_1(\控制器_1_alu_ctl ), .out_5(\n32位alu_1_out_5 ), .A(\n32_32寄存器_1_rs_out ), .B(multiplexer_2_out),
    .out_4(\n32位alu_1_out_4 ));
  \数据存储器  \u_数据存储器_1  (
    .MenRead(\控制器_1_memwrite ), .address(\n32位alu_1_out_5 ), .out_6(\数据存储器_1_out_6 ), .in_3(clck),
    .\input (\n32_32寄存器_1_rt_out ), .clear(clear_2));
  Multiplexer #(.select(1), .width(32), .disabled("Z"), .enable("false")) multiplexer_3 (
    .in0(\n32位alu_1_out_5 ), .in1(\数据存储器_1_out_6 ), .out(multiplexer_3_out), .sel(\控制器_1_memtoreg ));
endmodule
